# Fritzing sketch Receiver Scheme (saved by Fritzing 0.9.2b)
breadboards: 1

parts:
  Componente1 = Arduino Nano (Rev3.0)
  M1 = DC Motor
  Q9 = MOSFET-NCHANNEL [package=to220v]
  Q10 = Basic FET P-Channel [package="DPak [SMD]"]
  Q11 = MOSFET-NCHANNEL [package=to220v]
  Q12 = Basic FET P-Channel [package="DPak [SMD]"]
  M3 = DC Motor
  Q13 = MOSFET-NCHANNEL [package=to220v]
  Q14 = MOSFET-NCHANNEL [package=to220v]
  Q16 = Basic FET P-Channel [package="DPak [SMD]"]
  VCC1 = Battery block 9V
  Q15 = Basic FET P-Channel [package="DPak [SMD]"]

nets:
  N1: Componente1.GND, Q9.S, Q11.S, Q13.S, Q14.S, VCC1.-
  N2: Componente1.D2, Q11.G
  N3: Componente1.D3, Q12.Gate
  N4: Componente1.D4, Q9.G
  N5: Componente1.D5, Q10.Gate
  N6: Componente1.D6, Q14.G
  N7: Componente1.D7, Q16.Gate
  N8: Componente1.D8, Q13.G
  N9: Componente1.D9, Q15.Gate
  N10: Componente1.VIN, Q10.drain, Q12.drain, Q16.drain, VCC1.+, Q15.drain
  N11: M1.pin_1, Q10.source, Q11.D
  N12: M1.pin_2, Q9.D, Q12.source
  N13: M3.pin_1, Q14.D, Q15.source
  N14: M3.pin_2, Q13.D, Q16.source
